// Logisim project 7483.circ as structural Verilog: 2 circuits, main circuit IC 7483
// 7483
module IC_7483 (
  input  A4,
  input  B4,
  input  A3,
  input  B3,
  input  Vcc,
  input  Cin,
  input  A2,
  input  GND,
  input  B1,
  input  A1,
  input  B2,
  output S3,
  output S4,
  output S2,
  output Cout,
  output S1
);

  wire and_1_out, and_2_out, and_3_out, and_4_out, and_5_out, and_6_out, and_7_out, and_8_out, or_1_out,
       or_2_out, or_3_out, xor_1_out, xor_3_out, xor_5_out, xor_7_out;

  xor xor_1 (xor_1_out, A1, B1);
  and and_1 (and_1_out, xor_1_out, Cin);
  and and_2 (and_2_out, A1, B1);
  xor xor_2 (S1, xor_1_out, Cin);
  or or_1 (or_1_out, and_1_out, and_2_out);
  xor xor_3 (xor_3_out, A2, B2);
  xor xor_4 (S2, xor_3_out, or_1_out);
  and and_3 (and_3_out, xor_3_out, or_1_out);
  and and_4 (and_4_out, A2, B2);
  or or_2 (or_2_out, and_3_out, and_4_out);
  xor xor_5 (xor_5_out, A3, B3);
  xor xor_6 (S3, xor_5_out, or_2_out);
  and and_5 (and_5_out, xor_5_out, or_2_out);
  and and_6 (and_6_out, A3, B3);
  or or_3 (or_3_out, and_5_out, and_6_out);
  xor xor_7 (xor_7_out, A4, B4);
  xor xor_8 (S4, xor_7_out, or_3_out);
  and and_7 (and_7_out, xor_7_out, or_3_out);
  and and_8 (and_8_out, A4, B4);
  or or_4 (Cout, and_7_out, and_8_out);
endmodule

module Adder_Pairs (
  input  X0,
  input  Y0,
  input  Z0,
  input  X1,
  input  Y1,
  input  X2,
  input  Y2,
  input  X3,
  input  Y3,
  input  Z2,
  input  Z3,
  input  Z1,
  output S0,
  output S1,
  output S2,
  output S3,
  output Cout3,
  output Cout1,
  output Cout0,
  output Cout2
);

  IC_7483 Adder_1 (
    .A4(Y1), .A3(Z1), .B3(1'b1), .Vcc(1'b1), .S2(Cout0), .A2(1'b0), .B2(1'b0), .B4(X1), .S4(S1), .Cin(Z0),
    .Cout(Cout1), .GND(1'b0), .B1(Y0), .A1(X0), .S1(S0));  // open: S3
  IC_7483 Adder_2 (
    .A4(Y3), .A3(Z3), .B3(1'b1), .Vcc(1'b1), .S2(Cout2), .A2(1'b0), .B2(1'b0), .B4(X3), .S4(S3), .Cin(Z2),
    .Cout(Cout3), .GND(1'b0), .B1(Y2), .A1(X2), .S1(S2));  // open: S3
endmodule
