// Logisim project ALU_main_B2_G2.circ as structural Verilog: 1 circuit, main circuit main
module main (
  input  [3:0] B,
  input  [3:0] A,
  input  S2,
  input  S1,
  input  S0,
  output C,
  output S3,
  output S2_2,
  output S1_2,
  output S0_2,
  output S,
  output Z,
  output V
);

  wire adder_pairs_1_cout3, AND_3_p3, AND_3_p4, AND_3_p6, AND_3_p9, AND_3_p11, AND_3_p12, AND_3_p14,
       AND_4_p4, AND_4_p9, AND_4_p10, Decoder_1_p7, Decoder_1_p10, Decoder_1_p11, Decoder_1_p12,
       Decoder_1_p13, Decoder_1_p14, OR_2_p3, OR_2_p8, xi_1_x0, xi_1_x1, xi_1_x2, xi_1_x3, yi_1_y0, yi_1_y1,
       yi_1_y2, yi_1_y3, zi_1_man1;

  // _74238 Decoder_1: pin names not known; wires that end beside it: S0, S1, S2, 1'b0, 1'b0, 1'b1, Decoder_1_p7, 1'b0, 1'b1, Decoder_1_p10, Decoder_1_p11, Decoder_1_p12, Decoder_1_p13, Decoder_1_p14
  Xi xi_1 (
    .B0(B[0]), .B1(B[1]), .B2(B[2]), .B3(B[3]), .m7(Decoder_1_p7), .A0(A[0]), .m3(Decoder_1_p12), .A1(A[1]),
    .A2(A[2]), .A3(A[3]), .X0(xi_1_x0), .X1(xi_1_x1), .X2(xi_1_x2), .X3(xi_1_x3));  // open: NOT_13_6A, NOT_12_6Y, NOT_11_5A, NOT_10_5Y
  Yi yi_1 (
    .m1(Decoder_1_p11), .s0(S0), .m7(Decoder_1_p7), .B0(B[0]), .B1(B[1]), .Y3(yi_1_y3), .Y2(yi_1_y2),
    .B2(B[2]), .B3(B[3]), .Y0(yi_1_y0), .Y1(yi_1_y1));
  Zi zi_1 (
    .m0(Decoder_1_p10), .m4(Decoder_1_p13), .m1(Decoder_1_p11), .m3(Decoder_1_p12), .m5(Decoder_1_p14),
    .Man1(zi_1_man1));
  // _7408 AND_3: pin names not known; wires that end beside it: zi_1_man1, S0, AND_3_p3, AND_3_p4, zi_1_man1, AND_3_p6, 1'b0, 1'b1, AND_3_p9, zi_1_man1, AND_3_p11, AND_3_p12, zi_1_man1, AND_3_p14
  Adder_Pairs adder_pairs_1 (
    .X0(xi_1_x0), .Y0(yi_1_y0), .Z0(AND_3_p3), .X1(xi_1_x1), .Y1(yi_1_y1), .X2(xi_1_x2), .Y2(yi_1_y2),
    .X3(xi_1_x3), .Y3(yi_1_y3), .Z2(AND_3_p11), .Z3(AND_3_p14), .Cout0(AND_3_p4), .Cout2(AND_3_p12),
    .Z1(AND_3_p6), .S0(S0_2), .S1(S1_2), .S2(S2_2), .S3(S), .Cout3(adder_pairs_1_cout3), .Cout1(AND_3_p9));
  // _7432 OR_2: pin names not known; wires that end beside it: S0_2, S1_2, OR_2_p3, 1'b0, 1'b1, S2_2, S, OR_2_p8
  // _7408 AND_4: pin names not known; wires that end beside it: adder_pairs_1_cout3, zi_1_man1, C, AND_4_p4, zi_1_man1, V, 1'b0, 1'b1, AND_4_p9, AND_4_p10, Z
  // _7486 XOR_3: pin names not known; wires that end beside it: adder_pairs_1_cout3, AND_3_p12, AND_4_p4, OR_2_p3, 1'b1, AND_4_p9, 1'b0, 1'b1, OR_2_p8, 1'b1, AND_4_p10

  assign S3 = S;
endmodule
