// Logisim project Xi.circ as structural Verilog: 1 circuit, main circuit Xi
module Xi (
  input  NOT_11_5A,
  input  NOT_13_6A,
  input  B0,
  input  B1,
  input  B2,
  input  B3,
  input  m7,
  input  A0,
  input  m3,
  input  A1,
  input  A2,
  input  A3,
  output NOT_12_6Y,
  output NOT_10_5Y,
  output X0,
  output X1,
  output X2,
  output X3
);

  wire AND_1_p3, AND_1_p6, AND_1_p11, AND_1_p14, NOT_1_p2, NOT_1_p4, NOT_1_p6, NOT_1_p14, XOR_1_p3, XOR_1_p6,
       XOR_1_p11, XOR_1_p14;

  // _7404 NOT_1: pin names not known; wires that end beside it: B0, NOT_1_p2, B1, NOT_1_p4, B2, NOT_1_p6, 1'b0, 1'b1, NOT_13_6A, NOT_12_6Y, NOT_11_5A, NOT_10_5Y, B3, NOT_1_p14
  // _7408 AND_1: pin names not known; wires that end beside it: NOT_1_p2, m7, AND_1_p3, NOT_1_p4, m7, AND_1_p6, 1'b0, 1'b1, m7, NOT_1_p14, AND_1_p11, m7, NOT_1_p6, AND_1_p14
  // _7486 XOR_1: pin names not known; wires that end beside it: A0, m3, XOR_1_p3, A1, m3, XOR_1_p6, 1'b0, 1'b1, m3, A3, XOR_1_p11, m3, A2, XOR_1_p14
  // _7432 OR_1: pin names not known; wires that end beside it: AND_1_p3, XOR_1_p3, X0, AND_1_p6, XOR_1_p6, X1, 1'b0, 1'b1, AND_1_p11, XOR_1_p11, X3, AND_1_p14, XOR_1_p14, X2
endmodule
