// Logisim project Yi.circ as structural Verilog: 1 circuit, main circuit Yi
module Yi (
  input  m1,
  input  s0,
  input  B2,
  input  B3,
  input  m7,
  input  B0,
  input  B1,
  output Y0,
  output Y1,
  output Y3,
  output Y2
);

  wire AND_2_p3, AND_2_p6, AND_2_p11, AND_2_p14, NOT_1_p2, OR_2_p3, OR_2_p8;

  // _7404 NOT_1: pin names not known; wires that end beside it: s0, NOT_1_p2, 1'b0, 1'b1
  // _7432 OR_2: pin names not known; wires that end beside it: NOT_1_p2, m7, OR_2_p3, 1'b0, 1'b1, m1, OR_2_p3, OR_2_p8
  // _7408 AND_2: pin names not known; wires that end beside it: B0, OR_2_p8, AND_2_p3, B1, OR_2_p8, AND_2_p6, 1'b0, 1'b1, B2, OR_2_p8, AND_2_p11, B3, OR_2_p8, AND_2_p14
  // _7486 XOR_2: pin names not known; wires that end beside it: AND_2_p3, m7, Y0, AND_2_p6, m7, Y1, 1'b0, 1'b1, AND_2_p11, m7, Y2, AND_2_p14, m7, Y3
endmodule
