// Logisim project Zi.circ as structural Verilog: 1 circuit, main circuit Zi
module Zi (
  input  m0,
  input  m4,
  input  m1,
  input  m5,
  input  m3,
  output Man1
);

  wire OR_3_p3, OR_3_p6, OR_3_p11;

  // _7432 OR_3: pin names not known; wires that end beside it: m0, m4, OR_3_p3, m1, m3, OR_3_p6, 1'b0, 1'b1, OR_3_p6, OR_3_p3, OR_3_p11, OR_3_p11, m5, Man1
endmodule
