// Logisim project AllCircuits.circ as structural Verilog
module main (
  input  [31:0] A,
  input  [31:0] B,
  output [31:0] OUTPUT,
  output Underflow,
  output Overflow
);

  wire Exp_Comparator_x_y, flag_generator_1_overflow, flag_generator_2_overflow, signbitcomparator_1_sign_l,
       signbitcomparator_1_sign_s;
  wire [4:0] Exp_Comparator_shiftamount;
  wire [10:0] Exp_Comparator_larger_exponent, Normalizer_normalizedexponent;
  wire [30:0] _32_bit_ALU_alu_out;
  wire [31:0] Normalizer_2_normalizedfraction, Normalizer_normalizedfraction, Redwan_sign_handler_output,
       Right_Shifter_with_MUX_shiftedfraction, Right_Shifter_with_MUX_unshiftedfraction,
       Rounder_output_rounded_fraction, Sign_Handler_large_output, Sign_Handler_small_output;

  NormComparator Exp_Comparator (
    .X(A[30:20]), .Y(B[30:20]), .X_Y(Exp_Comparator_x_y), .Larger_Exponent(Exp_Comparator_larger_exponent),
    .ShiftAmount(Exp_Comparator_shiftamount));
  RightShifterWithMux Right_Shifter_with_MUX (
    .Fraction_A({4'b0001, A[19:0], {8{1'b0}}}), .Fraction_B({4'b0001, B[19:0], {8{1'b0}}}),
    .Selection_0A1B(Exp_Comparator_x_y), .ShiftAmount(Exp_Comparator_shiftamount),
    .ShiftedFraction(Right_Shifter_with_MUX_shiftedfraction),
    .UnshiftedFraction(Right_Shifter_with_MUX_unshiftedfraction));
  signHandler Redwan_sign_handler (
    .SignBit(OUTPUT[31]), .Fraction({OUTPUT[31], _32_bit_ALU_alu_out}), .Exponent(11'h1),
    .Output(Redwan_sign_handler_output));
  Normalizer Normalizer (
    .Fraction(Redwan_sign_handler_output), .Exponent(Exp_Comparator_larger_exponent),
    .NormalizedFraction(Normalizer_normalizedfraction), .NormalizedExponent(Normalizer_normalizedexponent));
  signHandler Sign_Handler_small (
    .SignBit(signbitcomparator_1_sign_s), .Fraction(Right_Shifter_with_MUX_shiftedfraction),
    .Exponent(A[30:20]), .Output(Sign_Handler_small_output));
  signHandler Sign_Handler_large (
    .SignBit(signbitcomparator_1_sign_l), .Fraction(Right_Shifter_with_MUX_unshiftedfraction),
    .Exponent(B[30:20]), .Output(Sign_Handler_large_output));
  Rounder Rounder (
    .INPUT_FRACTION(Normalizer_normalizedfraction), .OUTPUT_ROUNDED_FRACTION(Rounder_output_rounded_fraction));
  flag_generator flag_generator_1 (
    .Fraction(Normalizer_normalizedfraction), .Exponent(Normalizer_normalizedexponent),
    .Overflow(flag_generator_1_overflow));  // open: Underflow
  ALU_32bit _32_bit_ALU (
    .ALU_A_IN(Sign_Handler_small_output), .ALU_B_IN(Sign_Handler_large_output), .OP_CODE(3'b000),
    .ALU_OUT({OUTPUT[31], _32_bit_ALU_alu_out}));  // open: Z, N
  Normalizer Normalizer_2 (
    .Fraction(Rounder_output_rounded_fraction), .Exponent(Normalizer_normalizedexponent),
    .NormalizedFraction({Normalizer_2_normalizedfraction[31:28], OUTPUT[19:0], Normalizer_2_normalizedfraction[7:0]}),
    .NormalizedExponent(OUTPUT[30:20]));
  flag_generator flag_generator_2 (
    .Fraction({Normalizer_2_normalizedfraction[31:28], OUTPUT[19:0], Normalizer_2_normalizedfraction[7:0]}),
    .Exponent(OUTPUT[30:20]), .Underflow(Underflow), .Overflow(flag_generator_2_overflow));
  signBitComparator signbitcomparator_1 (
    .SignA(A[31]), .SignB(B[31]), .A_B(Exp_Comparator_x_y), .Sign_L(signbitcomparator_1_sign_l),
    .Sign_S(signbitcomparator_1_sign_s));
  or or_1 (Overflow, flag_generator_2_overflow, flag_generator_1_overflow);
endmodule

module SigShifter (
  input  [31:0] Fraction,
  output [31:0] NormalFraction,
  output IncDecSign,
  output [15:0] IncDecAmount
);

  wire bitfinder_1_found;
  wire [4:0] bitfinder_1_index;
  wire [10:0] multiplexer_1_out;
  wire [31:0] shifter_1_out, shifter_2_out;

  BitFinder #(.width(32), .\type ("high1")) bitfinder_1 (
    .in(Fraction), .index(bitfinder_1_index), .found(bitfinder_1_found));
  Multiplexer #(.width(11), .disabled(0), .enable("false")) multiplexer_1 (
    .in0({11{1'b0}}), .in1(11'h1c), .out(multiplexer_1_out), .sel(bitfinder_1_found));
  NormComparator normcomparator_1 (
    .X({{6{1'b0}}, bitfinder_1_index}), .Y(multiplexer_1_out), .X_Y(IncDecSign),
    .ShiftAmount(IncDecAmount[4:0]));  // open: Larger_Exponent
  Shifter #(.width(32), .shift("lr")) shifter_1 (.in(Fraction), .\dist (IncDecAmount[4:0]), .out(shifter_1_out));
  Shifter #(.width(32)) shifter_2 (.in(Fraction), .\dist (IncDecAmount[4:0]), .out(shifter_2_out));
  Multiplexer #(.width(32), .disabled(0), .enable("false")) multiplexer_2 (
    .in0(shifter_1_out), .in1(shifter_2_out), .out(NormalFraction), .sel(IncDecSign));

  assign IncDecAmount[15:5] = {11{1'b0}};

  // Notes on the sheet:
  //   Comp With 28
endmodule

module IncDec (
  input  Selection_0Inc1Dec,
  input  [15:0] Exponent,
  input  [15:0] AmountOfIncDec,
  output [15:0] NormalExponent
);

  wire [15:0] adder_1_out, subtractor_1_out;

  Adder #(.width(16)) adder_1 (.a(Exponent), .b(AmountOfIncDec), .out(adder_1_out));  // open: cin, cout
  Subtractor #(.width(16)) subtractor_1 (.a(Exponent), .b(AmountOfIncDec), .out(subtractor_1_out));  // open: bin, bout
  Multiplexer #(.width(16), .enable("false")) multiplexer_1 (
    .in0(adder_1_out), .in1(subtractor_1_out), .out(NormalExponent), .sel(Selection_0Inc1Dec));
endmodule

module ALU_32bit (
  input  [31:0] ALU_A_IN,
  input  [31:0] ALU_B_IN,
  input  [2:0] OP_CODE,
  output [31:0] ALU_OUT,
  output Z,
  output N
);

  wire [31:0] adder_1_out, and_1_out, multiplexer_1_out, multiplexer_2_out, multiplexer_3_out,
       multiplexer_4_out, not_1_out, or_1_out, shifter_1_out, shifter_2_out, subtractor_1_out, xor_1_out;

  Adder #(.width(32)) adder_1 (.a(ALU_A_IN), .b(ALU_B_IN), .out(adder_1_out));  // open: cin, cout
  Subtractor #(.width(32)) subtractor_1 (.a(ALU_A_IN), .b(ALU_B_IN), .out(subtractor_1_out));  // open: bin, bout
  assign and_1_out = ALU_A_IN & ALU_B_IN;  // AND_Gate and_1, 32 bits wide
  assign or_1_out = ALU_A_IN | ALU_B_IN;  // OR_Gate or_1, 32 bits wide
  assign not_1_out = ~ALU_A_IN;  // NOT_Gate not_1, 32 bits wide
  assign xor_1_out = ALU_A_IN ^ ALU_B_IN;  // XOR_Gate xor_1, 32 bits wide
  Shifter #(.width(32)) shifter_1 (.in(ALU_A_IN), .\dist (5'b00001), .out(shifter_1_out));
  Shifter #(.width(32), .shift("lr")) shifter_2 (.in(ALU_A_IN), .\dist (5'b00001), .out(shifter_2_out));
  Multiplexer #(.width(32), .enable("false")) multiplexer_1 (
    .in0(adder_1_out), .in1(subtractor_1_out), .out(multiplexer_1_out), .sel(OP_CODE[0]));
  Multiplexer #(.width(32), .enable("false")) multiplexer_2 (
    .in0(and_1_out), .in1(or_1_out), .out(multiplexer_2_out), .sel(OP_CODE[0]));
  Multiplexer #(.width(32), .enable("false")) multiplexer_3 (
    .in0(not_1_out), .in1(xor_1_out), .out(multiplexer_3_out), .sel(OP_CODE[0]));
  Multiplexer #(.width(32), .enable("false")) multiplexer_4 (
    .in0(shifter_1_out), .in1(shifter_2_out), .out(multiplexer_4_out), .sel(OP_CODE[0]));
  Multiplexer #(.select(2), .width(32), .enable("false")) multiplexer_5 (
    .in0(multiplexer_1_out), .in1(multiplexer_2_out), .in2(multiplexer_3_out), .in3(multiplexer_4_out),
    .out(ALU_OUT), .sel(OP_CODE[2:1]));
  nor nor_1 (Z, ALU_OUT[0], ALU_OUT[1], ALU_OUT[2], ALU_OUT[3], ALU_OUT[4], ALU_OUT[5], ALU_OUT[6], ALU_OUT[7], ALU_OUT[8], ALU_OUT[9], ALU_OUT[10], ALU_OUT[11], ALU_OUT[12], ALU_OUT[13], ALU_OUT[14], ALU_OUT[15], ALU_OUT[16], ALU_OUT[17], ALU_OUT[18], ALU_OUT[19], ALU_OUT[20], ALU_OUT[21], ALU_OUT[22], ALU_OUT[23], ALU_OUT[24], ALU_OUT[25], ALU_OUT[26], ALU_OUT[27], ALU_OUT[28], ALU_OUT[29], ALU_OUT[30], ALU_OUT[31]);

  assign N = ALU_OUT[31];
endmodule

module NormComparator (
  input  [10:0] X,
  input  [10:0] Y,
  output X_Y,
  output [10:0] Larger_Exponent,
  output [4:0] ShiftAmount
);

  wire alu_16bit_2_n;
  wire [10:0] multiplexer_2_out, negator_1_out;
  wire [10:5] multiplexer_3_out;
  wire [15:0] alu_16bit_1_alu_out;

  ALU_16bit alu_16bit_1 (
    .ALU_A_IN({{5{1'b0}}, X}), .ALU_B_IN({{5{1'b0}}, Y}), .OP_CODE(3'b001), .ALU_OUT(alu_16bit_1_alu_out),
    .N(X_Y));  // open: Z, All_one
  Multiplexer #(.width(11), .disabled(0), .enable("false")) multiplexer_1 (
    .in0(X), .in1(Y), .out(Larger_Exponent), .sel(X_Y));
  Negator #(.width(11)) negator_1 (.in(alu_16bit_1_alu_out[10:0]), .out(negator_1_out));
  Multiplexer #(.width(11), .disabled(0), .enable("false")) multiplexer_2 (
    .in0(alu_16bit_1_alu_out[10:0]), .in1(negator_1_out), .out(multiplexer_2_out), .sel(X_Y));
  ALU_16bit alu_16bit_2 (
    .ALU_A_IN({{5{1'b0}}, multiplexer_2_out}), .ALU_B_IN(16'h1f), .OP_CODE(3'b001), .N(alu_16bit_2_n));  // open: ALU_OUT, Z, All_one
  Multiplexer #(.width(11), .disabled(0), .enable("false")) multiplexer_3 (
    .in0(11'h1f), .in1(multiplexer_2_out), .out({multiplexer_3_out, ShiftAmount}), .sel(alu_16bit_2_n));

  // Notes on the sheet:
  //   Subtraction
  //   Detect Larger
  //   Take 2's Com. If Diff Is Neg 
  //   Max Shift Is 11111(31 Places)
endmodule

module ALU_16bit (
  input  [15:0] ALU_A_IN,
  input  [15:0] ALU_B_IN,
  input  [2:0] OP_CODE,
  output [15:0] ALU_OUT,
  output Z,
  output N,
  output All_one
);

  wire adder_1_cout;
  wire [15:0] adder_1_out, and_1_out, multiplexer_1_out, multiplexer_2_out, multiplexer_3_out,
       multiplexer_4_out, not_1_out, or_1_out, shifter_1_out, shifter_2_out, subtractor_1_out, xor_1_out;

  Adder #(.width(16)) adder_1 (.a(ALU_A_IN), .b(ALU_B_IN), .out(adder_1_out), .cout(adder_1_cout));  // open: cin
  Subtractor #(.width(16)) subtractor_1 (
    .a(ALU_A_IN), .b(ALU_B_IN), .out(subtractor_1_out), .bin(adder_1_cout));  // open: bout
  assign and_1_out = ALU_A_IN & ALU_B_IN;  // AND_Gate and_1, 16 bits wide
  assign or_1_out = ALU_A_IN | ALU_B_IN;  // OR_Gate or_1, 16 bits wide
  assign not_1_out = ~ALU_A_IN;  // NOT_Gate not_1, 16 bits wide
  assign xor_1_out = ALU_A_IN ^ ALU_B_IN;  // XOR_Gate xor_1, 16 bits wide
  Shifter #(.width(16), .shift("rl")) shifter_1 (.in(ALU_A_IN), .\dist (4'b0001), .out(shifter_1_out));
  Shifter #(.width(16), .shift("rr")) shifter_2 (.in(ALU_A_IN), .\dist (4'b0001), .out(shifter_2_out));
  Multiplexer #(.width(16), .enable("false")) multiplexer_1 (
    .in0(adder_1_out), .in1(subtractor_1_out), .out(multiplexer_1_out), .sel(OP_CODE[0]));
  Multiplexer #(.width(16), .enable("false")) multiplexer_2 (
    .in0(and_1_out), .in1(or_1_out), .out(multiplexer_2_out), .sel(OP_CODE[0]));
  Multiplexer #(.width(16), .enable("false")) multiplexer_3 (
    .in0(not_1_out), .in1(xor_1_out), .out(multiplexer_3_out), .sel(OP_CODE[0]));
  Multiplexer #(.width(16), .enable("false")) multiplexer_4 (
    .in0(shifter_1_out), .in1(shifter_2_out), .out(multiplexer_4_out), .sel(OP_CODE[0]));
  and and_2 (All_one, ALU_OUT[0], ALU_OUT[1], ALU_OUT[2], ALU_OUT[3], ALU_OUT[4], ALU_OUT[5], ALU_OUT[6], ALU_OUT[7], ALU_OUT[8], ALU_OUT[9], ALU_OUT[10]);
  Multiplexer #(.select(2), .width(16), .enable("false")) multiplexer_5 (
    .in0(multiplexer_1_out), .in1(multiplexer_2_out), .in2(multiplexer_3_out), .in3(multiplexer_4_out),
    .out(ALU_OUT), .sel(OP_CODE[2:1]));
  nor nor_1 (Z, ALU_OUT[0], ALU_OUT[1], ALU_OUT[2], ALU_OUT[3], ALU_OUT[4], ALU_OUT[5], ALU_OUT[6], ALU_OUT[7], ALU_OUT[8], ALU_OUT[9], ALU_OUT[10], ALU_OUT[11], ALU_OUT[12], ALU_OUT[13], ALU_OUT[14], ALU_OUT[15]);

  assign N = ALU_OUT[15];
endmodule

module Normalizer (
  input  [31:0] Fraction,
  input  [10:0] Exponent,
  output [31:0] NormalizedFraction,
  output [10:0] NormalizedExponent
);

  wire sigshifter_1_incdecsign;
  wire [15:0] sigshifter_1_incdecamount;
  wire [15:11] incdec_1_normalexponent;

  SigShifter sigshifter_1 (
    .Fraction(Fraction), .NormalFraction(NormalizedFraction), .IncDecSign(sigshifter_1_incdecsign),
    .IncDecAmount(sigshifter_1_incdecamount));
  IncDec incdec_1 (
    .Exponent({{5{1'b0}}, Exponent}), .AmountOfIncDec(sigshifter_1_incdecamount),
    .Selection_0Inc1Dec(sigshifter_1_incdecsign),
    .NormalExponent({incdec_1_normalexponent, NormalizedExponent}));
endmodule

module RightShifterWithMux (
  input  [31:0] Fraction_A,
  input  [31:0] Fraction_B,
  input  Selection_0A1B,
  input  [4:0] ShiftAmount,
  output [31:0] ShiftedFraction,
  output [31:0] UnshiftedFraction
);

  wire [31:0] multiplexer_1_out;

  Multiplexer #(.width(32), .enable("false")) multiplexer_1 (
    .in0(Fraction_B), .in1(Fraction_A), .out(multiplexer_1_out), .sel(Selection_0A1B));
  Multiplexer #(.width(32), .enable("false")) multiplexer_2 (
    .in0(Fraction_A), .in1(Fraction_B), .out(UnshiftedFraction), .sel(Selection_0A1B));
  Shifter #(.width(32), .shift("lr")) shifter_1 (.in(multiplexer_1_out), .\dist (ShiftAmount), .out(ShiftedFraction));
endmodule

module signHandler (
  input  SignBit,
  input  [31:0] Fraction,
  input  [10:0] Exponent,
  output [31:0] Output
);

  wire bitfinder_1_found;
  wire [31:0] multiplexer_1_out, negator_1_out;

  Negator #(.width(32)) negator_1 (.in(Fraction), .out(negator_1_out));
  BitFinder #(.width(11)) bitfinder_1 (.in(Exponent), .found(bitfinder_1_found));  // open: index
  Multiplexer #(.width(32), .enable("false")) multiplexer_1 (
    .in0(Fraction), .in1(negator_1_out), .out(multiplexer_1_out), .sel(SignBit));
  Multiplexer #(.width(32), .enable("false")) multiplexer_2 (
    .in0({32{1'b0}}), .in1(multiplexer_1_out), .out(Output), .sel(bitfinder_1_found));
endmodule

module Rounder (
  input  [31:0] INPUT_FRACTION,
  output [31:0] OUTPUT_ROUNDED_FRACTION
);

  wire n7432_1_p6, n7432_1_p9;
  wire [0:0] n7408_1_p4;
  wire [31:24] adder_1_out;

  // _7432 7432_1: pin names not known; wires that end beside it: INPUT_FRACTION[7], INPUT_FRACTION[6], INPUT_FRACTION[5], INPUT_FRACTION[5], INPUT_FRACTION[6], n7432_1_p6, n7432_1_p6, INPUT_FRACTION[8], n7432_1_p9, 1'b1
  // _7408 7408_1: pin names not known; wires that end beside it: 1'b0, n7432_1_p9, INPUT_FRACTION[7], n7408_1_p4[0], 1'b0, 1'b1
  Adder #(.width(32)) adder_1 (
    .a({{8{1'b0}}, INPUT_FRACTION[31:8]}), .b({{31{1'b0}}, n7408_1_p4[0]}),
    .out({adder_1_out, OUTPUT_ROUNDED_FRACTION[31:8]}));  // open: cin, cout

  assign OUTPUT_ROUNDED_FRACTION[7:0] = {8{1'b0}};

  // Notes on the sheet:
  //   G.(R + S + LastBit)
  //   Normalized 1
  //   GRS
endmodule

module signBitComparator (
  input  SignA,
  input  SignB,
  input  A_B,
  output Sign_L,
  output Sign_S
);

  Multiplexer #(.enable("false")) multiplexer_1 (.in0(SignA), .in1(SignB), .out(Sign_L), .sel(A_B));
  Multiplexer #(.enable("false")) multiplexer_2 (.in0(SignB), .in1(SignA), .out(Sign_S), .sel(A_B));
endmodule

module flag_generator (
  input  [31:0] Fraction,
  input  [10:0] Exponent,
  output Underflow,
  output Overflow
);

  wire alu_16bit_1_z, not_1_out;

  ALU_16bit alu_16bit_1 (
    .ALU_A_IN({{5{1'b0}}, Exponent}), .ALU_B_IN({16{1'b1}}), .OP_CODE(3'b010), .Z(alu_16bit_1_z),
    .All_one(Overflow));  // open: ALU_OUT, N
  not not_1 (not_1_out, Fraction[28]);
  or or_1 (Underflow, not_1_out, alu_16bit_1_z);
endmodule
