// Logisim project B2_G2_Mips.circ as structural Verilog
module Register_File (
  input  RegWrite,
  input  [3:0] SourceRegister1,
  input  [3:0] SourceRegister2,
  input  [3:0] DestinationRegister,
  input  [3:0] Write_Data,
  input  Clock,
  input  RegEn,
  output [3:0] ReadData_1,
  output Not_used,
  output [3:0] ReadData_2,
  output [3:0] zero,
  output [3:0] t0,
  output [3:0] t1,
  output [3:0] t2,
  output [3:0] t3,
  output [3:0] t4,
  output [3:0] sp
);

  wire decoder_1_out0, decoder_1_out1, decoder_1_out2, decoder_1_out3, decoder_1_out4, decoder_1_out5,
       decoder_1_out6, RegWriteActivator_2_p3, RegWriteActivator_2_p6, RegWriteActivator_2_p11,
       RegWriteActivator_p3, RegWriteActivator_p6, RegWriteActivator_p11, RegWriteActivator_p14;

  Decoder #(.select(3), .enable("false")) decoder_1 (
    .out0(decoder_1_out0), .out1(decoder_1_out1), .out2(decoder_1_out2), .out3(decoder_1_out3),
    .out4(decoder_1_out4), .out5(decoder_1_out5), .out6(decoder_1_out6), .out7(Not_used),
    .sel(DestinationRegister[2:0]));
  // _7408 RegWriteActivator: pin names not known; wires that end beside it: RegWrite, decoder_1_out0, RegWriteActivator_p3, RegWrite, decoder_1_out1, RegWriteActivator_p6, 1'b0, 1'b1, RegWrite, decoder_1_out2, RegWriteActivator_p11, RegWrite, decoder_1_out3, RegWriteActivator_p14
  // _7408 RegWriteActivator_2: pin names not known; wires that end beside it: RegWrite, decoder_1_out4, RegWriteActivator_2_p3, RegWrite, decoder_1_out5, RegWriteActivator_2_p6, 1'b0, 1'b1, RegWrite, decoder_1_out6, RegWriteActivator_2_p11, 1'b0, 1'b0
  Register #(.width(4)) u_zero (.D(Write_Data), .en(RegWriteActivator_p3), .Q(zero), .clk(Clock), .clr(RegEn));
  Register #(.width(4)) u_t0 (.D(Write_Data), .en(RegWriteActivator_p6), .Q(t0), .clk(Clock), .clr(RegEn));
  Register #(.width(4)) u_t1 (.D(Write_Data), .en(RegWriteActivator_p11), .Q(t1), .clk(Clock), .clr(RegEn));
  Register #(.width(4)) u_t2 (.D(Write_Data), .en(RegWriteActivator_p14), .Q(t2), .clk(Clock), .clr(RegEn));
  Register #(.width(4)) u_t3 (.D(Write_Data), .en(RegWriteActivator_2_p3), .Q(t3), .clk(Clock), .clr(RegEn));
  Register #(.width(4)) u_t4 (.D(Write_Data), .en(RegWriteActivator_2_p6), .Q(t4), .clk(Clock), .clr(RegEn));
  Register #(.width(4)) u_sp (.D(Write_Data), .en(RegWriteActivator_2_p11), .Q(sp), .clk(Clock), .clr(RegEn));
  Multiplexer #(.select(3), .width(4), .enable("false")) multiplexer_1 (
    .in0(zero), .in1(t0), .in2(t1), .in3(t2), .in4(t3), .in5(t4), .in6(sp), .out(ReadData_1),
    .sel(SourceRegister1[2:0]));  // open: in7
  Multiplexer #(.select(3), .width(4), .enable("false")) multiplexer_2 (
    .in0(zero), .in1(t0), .in2(t1), .in3(t2), .in4(t3), .in5(t4), .in6(sp), .out(ReadData_2),
    .sel(SourceRegister2[2:0]));  // open: in7

  // Notes on the sheet:
  //   Upper Wire : Write Data
  //   Lower wire : Register Enable
  //   CLOCK
  //   RegEn
endmodule
