// Logisim project MIPS_us.circ as structural Verilog: 2 circuits, main circuit main
module main (
  input  in_1,
  input  in_2,
  input  in_3,
  input  in_4,
  input  in_5,
  output [3:0] zero,
  output [3:0] t0,
  output [3:0] t1,
  output [3:0] zero_2,
  output [3:0] t2,
  output [3:0] t3,
  output [3:0] t4,
  output [3:0] sp
);

  wire Clk_out, control_unit_1_alusrc, control_unit_1_beq, control_unit_1_bneq, control_unit_1_jump,
       control_unit_1_memread, control_unit_1_memtoreg, control_unit_1_memwrite, control_unit_1_regdst,
       control_unit_1_regwrite, main_1_branch, main_2_zero;
  wire [2:0] control_unit_1_aluop;
  wire [3:0] main_2_a_2, multiplexer_3_out, multiplexer_4_out, multiplexer_5_out, ram_2_data,
       register_file_1_readdata_1, register_file_1_readdata_2;
  wire [7:0] adder_1_out, adder_2_out, bit_extender_1_out, multiplexer_1_out, multiplexer_2_out, PC_q;
  wire [15:0] ram_1_data;

  Register PC (.D(multiplexer_2_out), .en(in_1), .Q(PC_q), .clk(Clk_out), .clr(in_2));
  Clock Clk (.out(Clk_out));
  Adder adder_1 (.a(8'h1), .b(PC_q), .out(adder_1_out));  // open: cin, cout
  assign bit_extender_1_out = {{4{ram_1_data[3]}}, ram_1_data[3:0]};  // Bit_Extender bit_extender_1
  Adder adder_2 (.a(adder_1_out), .b(bit_extender_1_out), .out(adder_2_out));  // open: cin, cout
  RAM #(.dataWidth(16)) ram_1 (.addr(PC_q), .data(ram_1_data), .sel(1'b1), .clk(Clk_out), .ld(1'b1), .clr(in_3));
  Multiplexer #(.width(8), .enable("false")) multiplexer_1 (
    .in0(adder_1_out), .in1(adder_2_out), .out(multiplexer_1_out), .sel(main_1_branch));
  Multiplexer #(.width(8), .enable("false")) multiplexer_2 (
    .in0(multiplexer_1_out), .in1(ram_1_data[11:4]), .out(multiplexer_2_out), .sel(control_unit_1_jump));
  Control_Unit control_unit_1 (
    .OpCode(ram_1_data[15:12]), .Jump(control_unit_1_jump), .RegDst(control_unit_1_regdst),
    .Beq(control_unit_1_beq), .Bneq(control_unit_1_bneq), .MemWrite(control_unit_1_memwrite),
    .MemRead(control_unit_1_memread), .RegWrite(control_unit_1_regwrite), .MemToReg(control_unit_1_memtoreg),
    .ALUsrc(control_unit_1_alusrc), .ALUop(control_unit_1_aluop));
  Multiplexer #(.width(4), .enable("false")) multiplexer_3 (
    .in0(ram_1_data[7:4]), .in1(ram_1_data[3:0]), .out(multiplexer_3_out), .sel(control_unit_1_regdst));
  Mips_Branch_main main_1 (
    .zero(main_2_zero), .beq(control_unit_1_beq), .bneq(control_unit_1_bneq), .branch(main_1_branch));
  Register_File register_file_1 (
    .SourceRegister1(ram_1_data[11:8]), .SourceRegister2(ram_1_data[7:4]),
    .DestinationRegister(multiplexer_3_out), .Write_Data(multiplexer_5_out),
    .RegWrite(control_unit_1_regwrite), .Clock(Clk_out), .RegEn(in_4), .zero(zero), .t0(t0), .t1(t1),
    .t2(t2), .t3(t3), .t4(t4), .sp(sp), .ReadData_1(register_file_1_readdata_1),
    .ReadData_2(register_file_1_readdata_2));  // open: Not_used
  Multiplexer #(.width(4), .enable("false")) multiplexer_4 (
    .in0(register_file_1_readdata_2), .in1(ram_1_data[3:0]), .out(multiplexer_4_out),
    .sel(control_unit_1_alusrc));
  _4bitALU_main main_2 (
    .s2_s1_s0(control_unit_1_aluop), .A(register_file_1_readdata_1), .B(multiplexer_4_out), .A_2(main_2_a_2),
    .zero(main_2_zero));
  RAM #(.addrWidth(4), .dataWidth(4), .bus("separate")) ram_2 (
    .addr(main_2_a_2), .din(register_file_1_readdata_2), .data(ram_2_data), .str(control_unit_1_memwrite),
    .sel(1'b1), .clk(Clk_out), .ld(control_unit_1_memread), .clr(in_5));
  Multiplexer #(.width(4), .enable("false")) multiplexer_5 (
    .in0(main_2_a_2), .in1(ram_2_data), .out(multiplexer_5_out), .sel(control_unit_1_memtoreg));

  // Notes on the sheet:
  //   Instruction Memory
endmodule

// Control Unit
module Control_Unit (
  input  [3:0] OpCode,
  output [2:0] ALUop,
  output Jump,
  output RegDst,
  output ALUsrc,
  output MemWrite,
  output Beq,
  output RegWrite,
  output MemRead,
  output MemToReg,
  output Bneq
);

  ROM #(.addrWidth(4), .dataWidth(12)) rom_1 (
    .addr(OpCode), .data({Jump, RegDst, Beq, Bneq, MemWrite, MemRead, RegWrite, MemToReg, ALUsrc, ALUop}));  // open: sel

  // Notes on the sheet:
  //   contents of rom_1 (hex, n*v repeats v):
  //   29 423 422 421 203 7a 2e 2f 2b 2a 103 28 420 800 424 8a
endmodule
