// Logisim project Mips_Branch.circ as structural Verilog: 1 circuit, main circuit main
module main (
  input  zero,
  input  beq,
  input  bneq,
  output branch
);

  wire n7404_1_p2, n7408_1_p3, n7408_1_p6;

  // _7404 7404_1: pin names not known; wires that end beside it: zero, n7404_1_p2, 1'b0, 1'b1
  // _7408 7408_1: pin names not known; wires that end beside it: zero, beq, n7408_1_p3, n7404_1_p2, bneq, n7408_1_p6, 1'b0, 1'b1
  // _7432 7432_1: pin names not known; wires that end beside it: n7408_1_p6, n7408_1_p3, branch, 1'b0, 1'b1
endmodule
